// Logisim project ODV-3.circ as structural Verilog: 1 circuit, main circuit main
module main (
  input  [7:0] x2,
  input  [7:0] x1,
  input  x3,
  input  x1_2,
  input  x2_2,
  input  x3_2,
  output [7:0] out_7,
  output [7:0] out_8,
  output [7:0] out_9,
  output [7:0] out_10,
  output b,
  output d
);

  wire and_1_out, and_2_out, and_3_out, and_4_out, and_5_out, and_6_out, and_7_out, and_8_out, and_9_out,
       and_10_out, and_11_out, and_12_out, and_13_out, and_14_out, and_15_out, and_16_out, and_17_out,
       and_18_out, and_19_out, and_20_out, and_21_out, and_22_out, and_23_out, and_24_out, and_25_out,
       and_26_out, and_27_out, and_28_out, and_29_out, and_30_out, and_31_out, and_32_out, and_33_out,
       and_34_out, and_35_out, and_36_out, and_37_out, and_38_out, and_39_out, and_40_out, and_41_out,
       and_42_out, and_43_out, and_44_out, and_45_out, not_1_out, not_2_out, not_3_out, not_4_out, not_5_out,
       not_6_out, not_7_out, not_8_out, not_9_out, not_10_out, not_11_out, not_12_out, not_13_out,
       not_14_out, not_15_out, not_16_out, not_17_out, not_18_out, not_19_out, not_20_out, not_21_out,
       not_22_out, not_23_out, not_24_out, not_25_out, not_26_out, not_27_out, or_1_out, or_4_out, or_5_out,
       or_6_out, or_7_out, or_8_out, or_9_out, or_10_out, or_11_out, or_12_out, or_13_out, or_14_out,
       or_15_out, or_16_out, or_17_out, or_18_out, or_19_out;

  not not_1 (not_1_out, x1_2);
  not not_2 (not_2_out, x2_2);
  not not_3 (not_3_out, x3_2);
  and and_1 (and_1_out, x2_2, x3_2);
  and and_2 (and_2_out, not_1_out, x3_2);
  and and_3 (and_3_out, not_1_out, x2_2);
  or or_1 (or_1_out, x1_2, not_2_out, not_3_out);
  and and_4 (and_4_out, x1_2, not_2_out, not_3_out);
  or or_2 (b, and_1_out, and_2_out, and_3_out);
  and and_5 (and_5_out, b, or_1_out);
  or or_3 (d, and_5_out, and_4_out);
  not not_4 (not_4_out, x1[0]);
  not not_5 (not_5_out, x2[0]);
  not not_6 (not_6_out, x1[1]);
  not not_7 (not_7_out, x2[1]);
  not not_8 (not_8_out, x1[2]);
  not not_9 (not_9_out, x2[2]);
  not not_10 (not_10_out, x1[3]);
  not not_11 (not_11_out, x2[3]);
  not not_12 (not_12_out, x1[4]);
  not not_13 (not_13_out, x2[4]);
  not not_14 (not_14_out, x1[5]);
  not not_15 (not_15_out, x2[5]);
  not not_16 (not_16_out, x1[6]);
  not not_17 (not_17_out, x2[6]);
  not not_18 (not_18_out, x1[7]);
  not not_19 (not_19_out, x2[7]);
  not not_20 (not_20_out, x3);
  not not_21 (not_21_out, or_12_out);
  not not_22 (not_22_out, or_13_out);
  not not_23 (not_23_out, or_14_out);
  not not_24 (not_24_out, or_15_out);
  not not_25 (not_25_out, or_16_out);
  not not_26 (not_26_out, or_17_out);
  not not_27 (not_27_out, or_18_out);
  and and_6 (and_6_out, x2[0], x3);
  and and_7 (and_7_out, not_4_out, x3);
  and and_8 (and_8_out, not_4_out, x2[0]);
  or or_4 (or_4_out, x1[0], not_5_out, not_20_out);
  and and_9 (and_9_out, x1[0], not_5_out, not_20_out);
  and and_10 (and_10_out, x2[1], or_12_out);
  and and_11 (and_11_out, not_6_out, or_12_out);
  and and_12 (and_12_out, not_6_out, x2[1]);
  or or_5 (or_5_out, x1[1], not_7_out, not_21_out);
  and and_13 (and_13_out, x1[1], not_7_out, not_21_out);
  and and_14 (and_14_out, x2[2], or_13_out);
  and and_15 (and_15_out, not_8_out, or_13_out);
  and and_16 (and_16_out, not_8_out, x2[2]);
  or or_6 (or_6_out, x1[2], not_9_out, not_22_out);
  and and_17 (and_17_out, x1[2], not_9_out, not_22_out);
  and and_18 (and_18_out, x2[3], or_14_out);
  and and_19 (and_19_out, not_10_out, or_14_out);
  and and_20 (and_20_out, not_10_out, x2[3]);
  or or_7 (or_7_out, x1[3], not_11_out, not_23_out);
  and and_21 (and_21_out, x1[3], not_11_out, not_23_out);
  and and_22 (and_22_out, x2[4], or_15_out);
  and and_23 (and_23_out, not_12_out, or_15_out);
  and and_24 (and_24_out, not_12_out, x2[4]);
  or or_8 (or_8_out, x1[4], not_13_out, not_24_out);
  and and_25 (and_25_out, x1[4], not_13_out, not_24_out);
  and and_26 (and_26_out, x2[5], or_16_out);
  and and_27 (and_27_out, not_14_out, or_16_out);
  and and_28 (and_28_out, not_14_out, x2[5]);
  or or_9 (or_9_out, x1[5], not_15_out, not_25_out);
  and and_29 (and_29_out, x1[5], not_15_out, not_25_out);
  and and_30 (and_30_out, x2[6], or_17_out);
  and and_31 (and_31_out, not_16_out, or_17_out);
  and and_32 (and_32_out, not_16_out, x2[6]);
  or or_10 (or_10_out, x1[6], not_17_out, not_26_out);
  and and_33 (and_33_out, x1[6], not_17_out, not_26_out);
  and and_34 (and_34_out, x2[7], or_18_out);
  and and_35 (and_35_out, not_18_out, or_18_out);
  and and_36 (and_36_out, not_18_out, x2[7]);
  or or_11 (or_11_out, x1[7], not_19_out, not_27_out);
  and and_37 (and_37_out, x1[7], not_19_out, not_27_out);
  or or_12 (or_12_out, and_6_out, and_7_out, and_8_out);
  or or_13 (or_13_out, and_10_out, and_11_out, and_12_out);
  or or_14 (or_14_out, and_14_out, and_15_out, and_16_out);
  or or_15 (or_15_out, and_18_out, and_19_out, and_20_out);
  or or_16 (or_16_out, and_22_out, and_23_out, and_24_out);
  or or_17 (or_17_out, and_26_out, and_27_out, and_28_out);
  or or_18 (or_18_out, and_30_out, and_31_out, and_32_out);
  or or_19 (or_19_out, and_34_out, and_35_out, and_36_out);
  and and_38 (and_38_out, or_12_out, or_4_out);
  and and_39 (and_39_out, or_13_out, or_5_out);
  and and_40 (and_40_out, or_14_out, or_6_out);
  and and_41 (and_41_out, or_15_out, or_7_out);
  and and_42 (and_42_out, or_16_out, or_8_out);
  and and_43 (and_43_out, or_17_out, or_9_out);
  and and_44 (and_44_out, or_18_out, or_10_out);
  and and_45 (and_45_out, or_19_out, or_11_out);
  or or_20 (out_7[0], and_38_out, and_9_out);
  or or_21 (out_7[1], and_39_out, and_13_out);
  or or_22 (out_7[2], and_40_out, and_17_out);
  or or_23 (out_7[3], and_41_out, and_21_out);
  or or_24 (out_7[4], and_42_out, and_25_out);
  or or_25 (out_7[5], and_43_out, and_29_out);
  or or_26 (out_7[6], and_44_out, and_33_out);
  or or_27 (out_7[7], and_45_out, and_37_out);

  assign out_8 = x2;
  assign out_9 = out_7;
  assign out_10 = x1;

  // Notes on the sheet:
  //   x1     x2     x3     !x1    !x2    !x3
  //   x1     x2     x3     !x1    !x2    !x3
endmodule
