// Logisim project d8421.circ as structural Verilog: 1 circuit, main circuit main
module main (
  input  [3:0] in_1,
  output [3:0] out_2,
  output [3:0] out_3,
  output [3:0] out_4
);

  wire and_1_out, and_2_out, and_3_out, and_4_out, and_5_out, and_6_out, and_7_out, not_1_out, not_2_out,
       not_4_out;

  not not_1 (not_1_out, in_1[3]);
  not not_2 (not_2_out, in_1[2]);
  not not_3 (out_3[0], in_1[0]);
  not not_4 (not_4_out, in_1[1]);
  and and_1 (and_1_out, not_4_out, in_1[0]);
  and and_2 (and_2_out, in_1[1], out_3[0]);
  and and_3 (and_3_out, not_1_out, in_1[2], not_4_out);
  and and_4 (and_4_out, not_1_out, in_1[2], out_3[0]);
  and and_5 (and_5_out, in_1[1], in_1[0], not_2_out);
  and and_6 (and_6_out, in_1[3], not_2_out);
  and and_7 (and_7_out, in_1[1], in_1[0], not_1_out, in_1[2]);
  or or_1 (out_3[1], and_1_out, and_2_out);
  or or_2 (out_3[2], and_3_out, and_4_out, and_5_out);
  or or_3 (out_3[3], and_6_out, and_7_out);

  assign out_2 = in_1;
  assign out_4 = out_3;
endmodule
