// Logisim project 8_states_sum.circ as structural Verilog: 1 circuit, main circuit main
module main (
  input  V
);

  wire and_1_out, and_2_out, clock_1_out;
  wire [2:0] T1_q;

  Clock clock_1 (.out(clock_1_out));
  and and_1 (and_1_out, T1_q[1], T1_q[0], V);
  and and_2 (and_2_out, T1_q[0], V);
  T_Flip_Flop T3 (.clk(clock_1_out), .T(and_1_out), .Q(T1_q[2]));  // open: Qn, preset, reset, en
  T_Flip_Flop T2 (.clk(clock_1_out), .T(and_2_out), .Q(T1_q[1]));  // open: Qn, preset, reset, en
  T_Flip_Flop T1 (.clk(clock_1_out), .T(V), .Q(T1_q[0]));  // open: Qn, preset, reset, en
  // Probe on T1_q

  // Notes on the sheet:
  //   q3
  //   q2
  //   q1
  //   v
endmodule
